# Fritzing sketch Arduino-p13 (saved by Fritzing 0.9.2b)
breadboards: 1

parts:
  R1 = Resistor [tolerance=±5% resistance=220 package=THT]
  LED1 = LED - 5mm [color="Red (633nm)" package="5 mm [THT]"]
  Composant1 = Arduino Uno (Rev3)

nets:
  N1: R1.Pin_0, Composant1.D13/SCK
  N2: R1.Pin_1, LED1.anode
  N3: LED1.cathode, Composant1.GND
