# Fritzing sketch Arduino-p24 (saved by Fritzing 0.8.5b)
breadboards: 1

parts:
  R1 = Resistor [tolerance=±5% resistance=220 package=THT]
  R2 = Photocell (LDR) [package=THT]
  R9 = Resistor [tolerance=±5% resistance=10k package=THT]
  Piezo1 = Piezo Speaker - PC Mount [part_number=COM-07950]

nets:
  N1: R1.Pin_0, Piezo1.VCC
  N2: R2.pin_1, R9.Pin_0
  N3: R9.Pin_1, Piezo1.GND

custom parts:
  Piezo Speaker - PC Mount: This is a small 12mm round speaker that operates around the audible 2kHz range. You can use these speakers to create simple music or user interfaces. Each speaker is PTH solderable and requires an operating voltage of 3.5-5V with a mean current of 35mA max. These speakers also have a typical sound output of 95 dBA and a coil resistance of 42 ±6.3 ohms.
